# Fritzing sketch circuit_diagram (saved by Fritzing 1.0.5)

parts:
  Part1 = Arduino Mega 2560 (Rev3)
  L298N2 = L298N DC motor driver
  DC_Mot_Enc1 = DC Motor with two-phase hall-encoder [part_number=VT-E-G25A-06-177E]
  BAT1 = 24 battery [package=battery]

nets:
  N1: Part1.GND, DC_Mot_Enc1.pin4
  N2: Part1.5V, DC_Mot_Enc1.pin5
  N3: Part1.D2_PWM, DC_Mot_Enc1.pin6
  N4: Part1.D3_PWM, DC_Mot_Enc1.pin3
  N5: Part1.D4_PWM, L298N2.IN1
  N6: Part1.D5_PWM, L298N2.IN2
  N7: L298N2.OUT1, DC_Mot_Enc1.pin2
  N8: L298N2.OUT2, DC_Mot_Enc1.pin1
  N9: L298N2.GND, BAT1.-
  N10: L298N2.5V, BAT1.+

custom parts:
  L298N DC motor driver: 2x DC motor driver with 78M05 positive voltage regulator (7..35 V) L298N: max 46 V, 2 A Set 5 V Enable jumper to enable 5 V regultor (needed for the L298N) and +5 V output at screw terminal or supply external +5 V at screw terminal Set ENA and/or ENB to +5 V to enable motor permanently or supply ENA and/or ENB with PWM signal IN1 and IN2 set rotation directory for motor A (OUT1/OUT2) IN2 and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
  24 battery: 24V lead acid type battery, like the Husqvarna YTH2448 12V 35AH battery. This is the mini version 1/4 the size of the actual battery to be closer to typical breadboard parts (around 2in wide rathher than 7in). The pads in pcb are sized to accomidate up to 14ga wire (as these batterys will deliver high currents.)
